// Logisim project 1fa.circ as structural Verilog: 2 circuits, main circuit main
module main (
  input  c0,
  input  x0,
  input  y0,
  output z0,
  output c1
);

  wire and_1_out, and_2_out, not_1_out, or_1_out;

  or or_1 (or_1_out, x0, y0);
  not not_1 (not_1_out, c0);
  parity3 parity3_1 (.x(c0), .y(x0), .z(y0), .parity(z0));
  and and_1 (and_1_out, not_1_out, x0, y0);
  or or_2 (c1, and_1_out, and_2_out);
  and and_2 (and_2_out, c0, or_1_out);
endmodule

module parity3 (
  input  x,
  input  y,
  input  z,
  output parity
);

  wire and_1_out, and_2_out, and_3_out, and_4_out, not_1_out, not_2_out, not_3_out, not_4_out, not_5_out,
       not_6_out;

  not not_1 (not_1_out, y);
  not not_2 (not_2_out, y);
  not not_3 (not_3_out, x);
  not not_4 (not_4_out, z);
  not not_5 (not_5_out, x);
  not not_6 (not_6_out, y);
  and and_1 (and_1_out, x, not_1_out, not_2_out);
  and and_2 (and_2_out, not_3_out, y, not_4_out);
  and and_3 (and_3_out, not_5_out, not_6_out, z);
  and and_4 (and_4_out, x, y, z);
  or or_1 (parity, and_1_out, and_2_out, and_3_out, and_4_out);
endmodule
