// Logisim project 4fa.circ as structural Verilog: 3 circuits, main circuit 1fa
module _1fa (
  input  c0,
  input  x0,
  input  y0,
  output z0,
  output c1
);

  wire and_1_out, and_2_out, not_1_out, or_1_out;

  or or_1 (or_1_out, x0, y0);
  not not_1 (not_1_out, c0);
  parity3 parity3_1 (.x(c0), .y(x0), .z(y0), .parity(z0));
  and and_1 (and_1_out, not_1_out, x0, y0);
  or or_2 (c1, and_1_out, and_2_out);
  and and_2 (and_2_out, c0, or_1_out);
endmodule

module parity3 (
  input  x,
  input  y,
  input  z,
  output parity
);

  wire and_1_out, and_2_out, and_3_out, and_4_out, not_1_out, not_2_out, not_3_out, not_4_out, not_5_out,
       not_6_out;

  not not_1 (not_1_out, y);
  not not_2 (not_2_out, y);
  not not_3 (not_3_out, x);
  not not_4 (not_4_out, z);
  not not_5 (not_5_out, x);
  not not_6 (not_6_out, y);
  and and_1 (and_1_out, x, not_1_out, not_2_out);
  and and_2 (and_2_out, not_3_out, y, not_4_out);
  and and_3 (and_3_out, not_5_out, not_6_out, z);
  and and_4 (and_4_out, x, y, z);
  or or_1 (parity, and_1_out, and_2_out, and_3_out, and_4_out);
endmodule

module _4bit_adder (
  input  c0,
  input  x0,
  input  x1,
  input  x2,
  input  x3,
  input  y0,
  input  y1,
  input  y2,
  input  y3,
  output z0,
  output z1,
  output z2,
  output z3,
  output c4
);

  wire n1fa_1_c1, n1fa_2_c1, n1fa_3_c1;

  _1fa u_1fa_1 (.c0(c0), .x0(x0), .y0(y0), .z0(z0), .c1(n1fa_1_c1));
  _1fa u_1fa_2 (.c0(n1fa_1_c1), .x0(x1), .y0(y1), .z0(z1), .c1(n1fa_2_c1));
  _1fa u_1fa_3 (.c0(n1fa_2_c1), .x0(x2), .y0(y2), .z0(z2), .c1(n1fa_3_c1));
  _1fa u_1fa_4 (.c0(n1fa_3_c1), .x0(x3), .y0(y3), .z0(z3), .c1(c4));

  // Notes on the sheet:
  //   1fa
  //   1fa
  //   1fa
  //   1fa
endmodule
