// Logisim project less.circ as structural Verilog: 1 circuit, main circuit main
module main (
  input  x2,
  input  x1,
  input  x0,
  input  y2,
  input  y1,
  input  y0,
  input  x2_2,
  input  x1_2,
  input  x0_2,
  input  y2_2,
  input  y1_2,
  input  y0_2,
  output out_13
);

  wire and_1_out, and_2_out, and_3_out, and_4_out, and_5_out, not_1_out, not_2_out, not_3_out;

  not not_1 (not_1_out, x2_2);
  not not_2 (not_2_out, x1_2);
  not not_3 (not_3_out, x0_2);
  and and_1 (and_1_out, not_1_out, y2_2);
  and and_2 (and_2_out, not_2_out, y1_2);
  and and_3 (and_3_out, not_3_out, y0_2);
  and and_4 (and_4_out, and_1_out, and_2_out);
  and and_5 (and_5_out, and_2_out, and_3_out);
  or or_1 (out_13, and_4_out, and_2_out, and_5_out);
endmodule
