// Logisim project 1ha.circ as structural Verilog: 2 circuits, main circuit main
module main (
  input  x0,
  input  y0,
  output z0,
  output z1
);

  parity2 parity2_1 (.x(x0), .y(y0), .parity(z0));
  and and_1 (z1, x0, y0);
endmodule

module parity2 (
  input  x,
  input  y,
  output parity
);

  wire and_1_out, and_2_out, not_1_out, not_2_out;

  not not_1 (not_1_out, y);
  not not_2 (not_2_out, x);
  and and_1 (and_1_out, x, not_1_out);
  and and_2 (and_2_out, not_2_out, y);
  or or_1 (parity, and_1_out, and_2_out);
endmodule
