// Logisim project 2to1mux.circ as structural Verilog: 1 circuit, main circuit main
module main (
  input  line0,
  input  line1,
  input  select,
  output mux2
);

  wire and_1_out, and_2_out, not_1_out;

  not not_1 (not_1_out, select);
  and and_1 (and_1_out, line1, select);
  and and_2 (and_2_out, line0, not_1_out);
  or or_1 (mux2, and_2_out, and_1_out);
endmodule
