// Logisim project 4to1mux.circ as structural Verilog: 1 circuit, main circuit main
module main (
  input  line00,
  input  line01,
  input  line10,
  input  line11,
  input  select1,
  input  select0,
  output mux4
);

  wire and_1_out, and_2_out, and_3_out, and_4_out, and_5_out, and_6_out, not_1_out, not_2_out, not_3_out,
       or_1_out, or_2_out;

  not not_1 (not_1_out, select0);
  not not_2 (not_2_out, select0);
  and and_1 (and_1_out, not_1_out, line00);
  or or_1 (or_1_out, and_1_out, and_2_out);
  and and_2 (and_2_out, select0, line01);
  and and_3 (and_3_out, not_2_out, line10);
  and and_4 (and_4_out, select0, line11);
  not not_3 (not_3_out, select1);
  or or_2 (or_2_out, and_3_out, and_4_out);
  and and_5 (and_5_out, or_1_out, not_3_out);
  and and_6 (and_6_out, or_2_out, select1);
  or or_3 (mux4, and_5_out, and_6_out);
endmodule
