// Logisim project xor2.circ as structural Verilog: 1 circuit, main circuit main
module main (
  input  x,
  input  y,
  output xor2
);

  wire and_1_out, and_2_out, not_1_out, not_2_out;

  and and_1 (and_1_out, x, not_1_out);
  not not_1 (not_1_out, y);
  not not_2 (not_2_out, x);
  and and_2 (and_2_out, not_2_out, y);
  or or_1 (xor2, and_1_out, and_2_out);
endmodule
